# Fritzing sketch uplift-prototype (saved by Fritzing 0.9.9b)
breadboards: 1

parts:
  Mod1 = Amica NodeMCU DevKit 1.0
  U1 = PCF8574 [package="DIP16 [THT]"]
  Part2 = I2C level shifter bidirectional
  Part3 = I2C level shifter bidirectional

nets:
  N1: Mod1.pin1, Mod1.pin_10, Mod1.pin_26, U1.VCC, Part2.LV, Part3.LV
  GND: Mod1.pin2, Mod1.pin_9, Mod1.pin_25, Mod1.pin_29, U1.A0, U1.A1, U1.A2, U1.GND, Part2.GND, Part3.GND, Part3.HV2
  N2: Mod1.pin6, Part3.LV4
  N3: Mod1.pin7, Part3.LV3
  N4: Mod1.pin8, Part3.LV2
  N5: Mod1.pin_13, U1.SDA
  N6: Mod1.pin_14, U1.SCL
  N7: U1.P0, Part2.LV1
  N8: U1.P1, Part2.LV2
  N9: U1.P2, Part2.LV3
  N10: U1.P3, Part2.LV4
  N11: U1.P7, Part3.LV1
  N12: Part2.HV, Part2.HV4, Part3.HV

custom parts:
  Amica NodeMCU DevKit 1.0: Amica NodeMCU DevKit 1.0 Development Kit based on ESP8266 ESP-12E, integating GPIO, PWM, IIC, 1-Wire and ADC all in one board. Links: NodeMCU information page Github
